// Logisim project TP1.circ as structural Verilog: 3 circuits, main circuit main
module main (
  input  in_1,
  input  [3:0] in_2,
  input  [3:0] in_3,
  input  [3:0] in_4,
  input  in_5,
  input  in_6,
  input  [31:0] in_7,
  input  [1:0] in_8
);

  wire [31:0] alu_1_sortie, banc_reg_1_valreg0, banc_reg_1_valreg1, multiplexer_1_out;

  banc_reg banc_reg_1 (
    .clk(in_1), .ValEcriture(alu_1_sortie), .IndReg0(in_2), .IndReg1(in_3), .IndRegEcr(in_4), .SigEcr(in_5),
    .ValReg0(banc_reg_1_valreg0), .Valreg1(banc_reg_1_valreg1));  // open: R15_in
  // Probe on banc_reg_1_valreg1
  Multiplexer #(.width(32)) multiplexer_1 (.in0(banc_reg_1_valreg1), .in1(in_7), .out(multiplexer_1_out), .sel(in_6));
  ALU alu_1 (.Op1(banc_reg_1_valreg0), .Op2(multiplexer_1_out), .Sel(in_8), .Sortie(alu_1_sortie));  // open: NZCV
endmodule

module decodeur (
  input  [31:0] Instr,
  output [3:0] Rs1,
  output [3:0] Rs2,
  output [3:0] Rd,
  output [7:0] Imm,
  output [3:0] Rot,
  output Imm_reg,
  output [1:0] Op
);

  decodeur_opcode decodeur_opcode_1 (.OpCode(Instr[24:21]), .Op(Op));

  assign Imm = Instr[7:0];
  assign Imm_reg = Instr[25];
  assign Rd = Instr[15:12];
  assign Rot = Instr[11:8];
  assign Rs1 = Instr[19:16];
  assign Rs2 = Instr[3:0];
endmodule

module decodeur_opcode (
  input  [3:0] OpCode,
  output [1:0] Op
);

  wire and_1_out, not_1_out;

  not not_1 (not_1_out, OpCode[3]);
  and and_1 (and_1_out, OpCode[2], not_1_out);
  or or_1 (Op[0], OpCode[0], OpCode[1]);
  or or_2 (Op[1], OpCode[1], and_1_out);
endmodule
